// Logisim project knight-rider-jk.circ as structural Verilog
module main (
);

  wire clock_1_out, j_k_ff_1_qn, j_k_ff_2_qn, j_k_ff_3_qn, j_k_ff_4_qn, j_k_ff_5_qn, j_k_ff_6_qn,
       j_k_ff_7_qn, j_k_ff_8_qn, j_k_ff_9_qn, j_k_ff_10_qn, j_k_ff_11_qn, j_k_ff_12_qn, j_k_ff_13_qn,
       j_k_ff_14_qn, not_1_out, not_2_out, or_1_out, or_2_out, or_3_out, or_4_out, or_5_out, or_6_out,
       or_7_out, or_8_out, or_9_out, undriven, undriven_2;
  wire [7:0] j_k_ff_1_q, j_k_ff_2_q;

  Clock clock_1 (.out(clock_1_out));
  not not_1 (not_1_out, or_1_out);
  not not_2 (not_2_out, j_k_ff_1_q[7]);
  J_K_Flip_Flop j_k_ff_1 (
    .J(or_1_out), .clk(clock_1_out), .K(not_1_out), .Q(j_k_ff_1_q[0]), .Qn(j_k_ff_1_qn), .reset(undriven));  // open: preset, en
  J_K_Flip_Flop j_k_ff_2 (
    .J(j_k_ff_1_q[7]), .clk(clock_1_out), .K(not_2_out), .Q(j_k_ff_2_q[0]), .Qn(j_k_ff_2_qn),
    .reset(undriven_2));  // open: preset, en
  J_K_Flip_Flop j_k_ff_3 (
    .J(j_k_ff_1_q[0]), .clk(clock_1_out), .K(j_k_ff_1_qn), .Q(j_k_ff_1_q[1]), .Qn(j_k_ff_3_qn),
    .reset(undriven));  // open: preset, en
  J_K_Flip_Flop j_k_ff_4 (
    .J(j_k_ff_2_q[0]), .clk(clock_1_out), .K(j_k_ff_2_qn), .Q(j_k_ff_2_q[1]), .Qn(j_k_ff_4_qn),
    .reset(undriven_2));  // open: preset, en
  J_K_Flip_Flop j_k_ff_5 (
    .J(j_k_ff_1_q[1]), .clk(clock_1_out), .K(j_k_ff_3_qn), .Q(j_k_ff_1_q[2]), .Qn(j_k_ff_5_qn),
    .reset(undriven));  // open: preset, en
  J_K_Flip_Flop j_k_ff_6 (
    .J(j_k_ff_2_q[1]), .clk(clock_1_out), .K(j_k_ff_4_qn), .Q(j_k_ff_2_q[2]), .Qn(j_k_ff_6_qn),
    .reset(undriven_2));  // open: preset, en
  J_K_Flip_Flop j_k_ff_7 (
    .J(j_k_ff_1_q[2]), .clk(clock_1_out), .K(j_k_ff_5_qn), .Q(j_k_ff_1_q[3]), .Qn(j_k_ff_7_qn),
    .reset(undriven));  // open: preset, en
  J_K_Flip_Flop j_k_ff_8 (
    .J(j_k_ff_2_q[2]), .clk(clock_1_out), .K(j_k_ff_6_qn), .Q(j_k_ff_2_q[3]), .Qn(j_k_ff_8_qn),
    .reset(undriven_2));  // open: preset, en
  J_K_Flip_Flop j_k_ff_9 (
    .J(j_k_ff_1_q[3]), .clk(clock_1_out), .K(j_k_ff_7_qn), .Q(j_k_ff_1_q[4]), .Qn(j_k_ff_9_qn),
    .reset(undriven));  // open: preset, en
  J_K_Flip_Flop j_k_ff_10 (
    .J(j_k_ff_2_q[3]), .clk(clock_1_out), .K(j_k_ff_8_qn), .Q(j_k_ff_2_q[4]), .Qn(j_k_ff_10_qn),
    .reset(undriven_2));  // open: preset, en
  J_K_Flip_Flop j_k_ff_11 (
    .J(j_k_ff_1_q[4]), .clk(clock_1_out), .K(j_k_ff_9_qn), .Q(j_k_ff_1_q[5]), .Qn(j_k_ff_11_qn),
    .reset(undriven));  // open: preset, en
  J_K_Flip_Flop j_k_ff_12 (
    .J(j_k_ff_1_q[5]), .clk(clock_1_out), .K(j_k_ff_11_qn), .Q(j_k_ff_1_q[6]), .Qn(j_k_ff_12_qn),
    .reset(undriven));  // open: preset, en
  J_K_Flip_Flop j_k_ff_13 (
    .J(j_k_ff_2_q[4]), .clk(clock_1_out), .K(j_k_ff_10_qn), .Q(j_k_ff_2_q[5]), .Qn(j_k_ff_13_qn),
    .reset(undriven_2));  // open: preset, en
  J_K_Flip_Flop j_k_ff_14 (
    .J(j_k_ff_2_q[5]), .clk(clock_1_out), .K(j_k_ff_13_qn), .Q(j_k_ff_2_q[6]), .Qn(j_k_ff_14_qn),
    .reset(undriven_2));  // open: preset, en
  J_K_Flip_Flop j_k_ff_15 (
    .J(j_k_ff_1_q[6]), .clk(clock_1_out), .K(j_k_ff_12_qn), .Q(j_k_ff_1_q[7]), .reset(undriven));  // open: Qn, preset, en
  J_K_Flip_Flop j_k_ff_16 (
    .J(j_k_ff_2_q[6]), .clk(clock_1_out), .K(j_k_ff_14_qn), .Q(j_k_ff_2_q[7]), .reset(undriven_2));  // open: Qn, preset, en
  buf or_1 (or_1_out, j_k_ff_2_q[7]);  // OR_Gate
  or or_2 (or_2_out, j_k_ff_2_q[7], j_k_ff_1_q[0]);
  or or_3 (or_3_out, j_k_ff_2_q[6], j_k_ff_1_q[1]);
  or or_4 (or_4_out, j_k_ff_2_q[4], j_k_ff_1_q[3]);
  or or_5 (or_5_out, j_k_ff_2_q[5], j_k_ff_1_q[2]);
  LED led_1 (.in(or_5_out));
  LED led_2 (.in(or_2_out));
  LED led_3 (.in(or_3_out));
  LED led_4 (.in(or_4_out));
  or or_6 (or_6_out, j_k_ff_2_q[3], j_k_ff_1_q[4]);
  LED led_5 (.in(or_8_out));
  LED led_6 (.in(or_9_out));
  LED led_7 (.in(or_6_out));
  LED led_8 (.in(or_7_out));
  or or_7 (or_7_out, j_k_ff_2_q[2], j_k_ff_1_q[5]);
  or or_8 (or_8_out, j_k_ff_2_q[1], j_k_ff_1_q[6]);
  or or_9 (or_9_out, j_k_ff_2_q[0], j_k_ff_1_q[7]);

  // Notes on the sheet:
  //   LAST
  //   CLK
  //   IN
  //   CLK
  //   LAST
  //   IN
endmodule
