// Logisim project onr-training-broken.circ as structural Verilog: 8 circuits, main circuit Ex: Module Master
module main (
);

  wire j_k_ff_1_q, j_k_ff_1_qn, j_k_ff_2_q, j_k_ff_2_qn, j_k_ff_3_q, j_k_ff_3_qn, j_k_ff_4_q, j_k_ff_4_qn,
       j_k_ff_5_q, j_k_ff_5_qn, j_k_ff_6_q, j_k_ff_6_qn, j_k_ff_7_q, j_k_ff_7_qn, not_1_out, or_1_out,
       or_2_out, or_3_out, or_4_out, or_5_out, undriven, undriven_2, undriven_3, undriven_4, undriven_5,
       undriven_6, undriven_7, undriven_8, undriven_9, undriven_10, undriven_11, undriven_12, undriven_13,
       undriven_14, undriven_15;

  or or_1 (or_1_out, undriven, undriven_4);
  not not_1 (not_1_out, or_1_out);
  J_K_Flip_Flop j_k_ff_1 (
    .J(or_1_out), .clk(undriven_5), .K(not_1_out), .Q(j_k_ff_1_q), .Qn(j_k_ff_1_qn), .reset(undriven_6));  // open: preset, en
  or or_2 (or_2_out, j_k_ff_1_q, undriven_2);
  J_K_Flip_Flop j_k_ff_2 (
    .J(j_k_ff_1_q), .clk(undriven_5), .K(j_k_ff_1_qn), .Q(j_k_ff_2_q), .Qn(j_k_ff_2_qn), .reset(undriven_6));  // open: preset, en
  or or_3 (or_3_out, j_k_ff_2_q, undriven_3);
  J_K_Flip_Flop j_k_ff_3 (
    .J(j_k_ff_2_q), .clk(undriven_5), .K(j_k_ff_2_qn), .Q(j_k_ff_3_q), .Qn(j_k_ff_3_qn), .reset(undriven_6));  // open: preset, en
  J_K_Flip_Flop j_k_ff_4 (
    .J(undriven_8), .clk(undriven_7), .K(undriven_9), .Q(j_k_ff_4_q), .Qn(j_k_ff_4_qn));  // open: preset, en, reset
  or or_4 (or_4_out, undriven_8, undriven_10);
  J_K_Flip_Flop j_k_ff_5 (
    .J(j_k_ff_4_q), .clk(undriven_7), .K(j_k_ff_4_qn), .Q(j_k_ff_5_q), .Qn(j_k_ff_5_qn));  // open: preset, en, reset
  J_K_Flip_Flop j_k_ff_6 (
    .J(undriven_12), .clk(undriven_11), .K(undriven_13), .Q(j_k_ff_6_q), .Qn(j_k_ff_6_qn));  // open: preset, en, reset
  or or_5 (or_5_out, undriven_14, undriven_15);
  J_K_Flip_Flop j_k_ff_7 (
    .J(j_k_ff_6_q), .clk(undriven_11), .K(j_k_ff_6_qn), .Q(j_k_ff_7_q), .Qn(j_k_ff_7_qn));  // open: preset, en, reset

  // Notes on the sheet:
  //   Module 1
  //   Module 2
  //   Module 3
endmodule

module Module_1 (
  input  CLK,
  input  PST,
  input  IN,
  input  CLR,
  input  L7,
  input  L6,
  output Q,
  output QN,
  output FF0,
  output FF1,
  output LED1,
  output LED0
);

  wire j_k_ff_1_qn, not_1_out, or_1_out;

  or or_1 (or_1_out, PST, IN);
  not not_1 (not_1_out, or_1_out);
  J_K_Flip_Flop j_k_ff_1 (
    .J(or_1_out), .clk(CLK), .K(not_1_out), .Q(FF0), .Qn(j_k_ff_1_qn), .reset(CLR));  // open: preset, en
  or or_2 (LED0, FF0, L7);
  J_K_Flip_Flop j_k_ff_2 (.J(FF0), .clk(CLK), .K(j_k_ff_1_qn), .Q(FF1), .Qn(QN), .reset(CLR));  // open: preset, en
  or or_3 (LED1, FF1, L6);

  assign Q = FF1;

  // Notes on the sheet:
  //   Module 1
endmodule

module Module_2 (
  input  CLK,
  input  J,
  input  K,
  input  CLR,
  input  L5,
  output Q,
  output QN,
  output FF2,
  output FF3,
  output LED2
);

  wire j_k_ff_1_qn, j_k_ff_2_qn;

  J_K_Flip_Flop j_k_ff_1 (.J(J), .clk(CLK), .K(K), .Q(FF2), .Qn(j_k_ff_1_qn), .reset(CLR));  // open: preset, en
  or or_1 (LED2, FF2, L5);
  J_K_Flip_Flop j_k_ff_2 (
    .J(FF2), .clk(CLK), .K(j_k_ff_1_qn), .Q(FF3), .Qn(j_k_ff_2_qn), .reset(CLR));  // open: preset, en
  J_K_Flip_Flop j_k_ff_3 (.J(FF3), .clk(CLK), .K(j_k_ff_2_qn), .Q(Q), .Qn(QN), .reset(CLR));  // open: preset, en

  // Notes on the sheet:
  //   Module 2
endmodule

module Module_3 (
  input  CLK,
  input  J,
  input  K,
  input  CLR,
  input  L4,
  output OUT,
  output OUTN,
  output FF4,
  output FF5,
  output FF6,
  output LED3
);

  wire j_k_ff_1_qn, j_k_ff_2_qn;

  J_K_Flip_Flop j_k_ff_1 (.J(J), .clk(CLK), .K(K), .Q(FF4), .Qn(j_k_ff_1_qn), .reset(CLR));  // open: preset, en
  or or_1 (LED3, FF4, L4);
  J_K_Flip_Flop j_k_ff_2 (
    .J(FF4), .clk(CLK), .K(j_k_ff_1_qn), .Q(FF6), .Qn(j_k_ff_2_qn), .reset(CLR));  // open: preset, en
  J_K_Flip_Flop j_k_ff_3 (.J(FF6), .clk(CLK), .K(j_k_ff_2_qn), .Q(OUT), .Qn(OUTN), .reset(CLK));  // open: preset, en

  assign FF5 = FF4;

  // Notes on the sheet:
  //   Module 3
endmodule

module Master (
  input  M1_LED0,
  input  M1_LED1,
  input  M2_LED2,
  input  M3_LED3,
  input  CLK,
  input  M1_FF0,
  input  M1_FF1,
  input  M2_FF2,
  input  M1_Q,
  input  IN,
  input  M3_QN,
  input  M1_QN,
  input  M3_FF4,
  input  M2_Q,
  input  CLR,
  input  M2_QN,
  input  M3_Q,
  input  M3_FF5,
  input  M2_FF3,
  input  M3_FF6,
  output LED0,
  output LED1,
  output LED2,
  output LED3,
  output M1_CLK,
  output M2_CLK,
  output M3_CLK,
  output M2_J,
  output M1_IN,
  output M2_K,
  output M3_J,
  output M1_CLR,
  output M3_K,
  output M2_CLR,
  output M3_CLR,
  output M1_PST,
  output M1_L6,
  output M1_L7,
  output M3_L4,
  output M2_L5
);


  assign LED0 = M1_LED0;
  assign LED1 = M1_LED1;
  assign LED2 = M2_LED2;
  assign LED3 = M3_LED3;
  assign M1_CLK = CLK;
  assign M1_CLR = CLR;
  assign M1_IN = IN;
  assign M1_L6 = M3_Q;
  assign M1_L7 = M3_FF5;
  assign M1_PST = M3_Q;
  assign M2_CLK = CLK;
  assign M2_CLR = CLR;
  assign M2_J = M1_Q;
  assign M2_K = M1_QN;
  assign M2_L5 = M3_FF6;
  assign M3_CLK = CLK;
  assign M3_CLR = CLR;
  assign M3_J = M2_Q;
  assign M3_K = M2_QN;
  assign M3_L4 = M2_FF3;

  // Notes on the sheet:
  //   Unused Inputs
  //   Module Maps
  //   Global Inputs
endmodule

module Ex__Module_Master (
);

  wire button_1_out, button_2_out, clock_1_out, master_1_led0, master_1_led1, master_1_led2, master_1_led3,
       master_1_m1_clk, master_1_m1_clr, master_1_m1_in, master_1_m1_l6, master_1_m1_l7, master_1_m1_pst,
       master_1_m2_clk, master_1_m2_clr, master_1_m2_j, master_1_m2_k, master_1_m2_l5, master_1_m3_clk,
       master_1_m3_clr, master_1_m3_j, master_1_m3_k, master_1_m3_l4, module_1_1_ff0, module_1_1_ff1,
       module_1_1_led0, module_1_1_led1, module_1_1_q, module_1_1_qn, module_2_1_ff2, module_2_1_ff3,
       module_2_1_led2, module_2_1_q, module_2_1_qn, module_3_1_ff4, module_3_1_ff5, module_3_1_ff6,
       module_3_1_led3, module_3_1_out, module_3_1_outn;

  Clock clock_1 (.out(clock_1_out));
  Button button_1 (.out(button_1_out));
  Button button_2 (.out(button_2_out));
  Module_1 module_1_1 (
    .CLK(master_1_m1_clk), .CLR(master_1_m1_clr), .L7(master_1_m1_l6), .L6(master_1_m1_l7), .Q(module_1_1_q),
    .QN(module_1_1_qn), .FF0(module_1_1_ff0), .FF1(module_1_1_ff1), .LED1(module_1_1_led1),
    .LED0(module_1_1_led0), .PST(master_1_m1_pst), .IN(master_1_m1_in));
  Master master_1 (
    .M1_LED0(module_1_1_led0), .CLK(clock_1_out), .M1_LED1(module_1_1_led1), .M2_LED2(module_2_1_led2),
    .M3_LED3(module_3_1_led3), .IN(button_1_out), .CLR(button_2_out), .M1_FF0(module_1_1_ff0),
    .M1_Q(module_1_1_q), .M1_FF1(module_1_1_ff1), .M1_QN(module_1_1_qn), .M2_FF2(module_2_1_ff2),
    .M2_Q(module_2_1_q), .M3_QN(module_3_1_outn), .M2_QN(module_2_1_qn), .M3_FF4(module_3_1_ff4),
    .M3_Q(module_3_1_out), .M3_FF5(module_3_1_ff6), .M2_FF3(module_2_1_ff3), .M3_FF6(module_3_1_ff5),
    .LED0(master_1_led0), .M1_CLK(master_1_m1_clk), .LED1(master_1_led1), .M2_CLK(master_1_m2_clk),
    .LED2(master_1_led2), .M3_CLK(master_1_m3_clk), .LED3(master_1_led3), .M1_IN(master_1_m1_in),
    .M1_CLR(master_1_m1_clr), .M2_CLR(master_1_m2_clr), .M3_CLR(master_1_m3_clr), .M2_J(master_1_m2_j),
    .M2_K(master_1_m2_k), .M3_J(master_1_m3_j), .M3_K(master_1_m3_k), .M1_PST(master_1_m1_pst),
    .M1_L6(master_1_m1_l6), .M1_L7(master_1_m1_l7), .M3_L4(master_1_m3_l4), .M2_L5(master_1_m2_l5));
  LED led_1 (.in(master_1_led3));
  LED led_2 (.in(master_1_led0));
  LED led_3 (.in(master_1_led2));
  LED led_4 (.in(master_1_led1));
  Module_2 module_2_1 (
    .CLK(master_1_m2_clk), .J(master_1_m2_j), .K(master_1_m2_k), .CLR(master_1_m2_clr), .L5(master_1_m2_l5),
    .Q(module_2_1_q), .FF2(module_2_1_ff2), .LED2(module_2_1_led2), .QN(module_2_1_qn), .FF3(module_2_1_ff3));
  Module_3 module_3_1 (
    .CLK(master_1_m3_clk), .J(master_1_m3_j), .K(master_1_m3_k), .CLR(master_1_m3_clr), .L4(master_1_m3_l4),
    .OUT(module_3_1_out), .OUTN(module_3_1_outn), .LED3(module_3_1_led3), .FF6(module_3_1_ff6),
    .FF5(module_3_1_ff5), .FF4(module_3_1_ff4));
endmodule

module Ex__Module_Hookup (
);

  wire button_1_out, button_2_out, clock_1_out, module_1_1_led0, module_1_1_led1, module_1_1_q,
       module_1_1_qn, module_2_1_ff3, module_2_1_led2, module_2_1_q, module_2_1_qn, module_3_1_ff5,
       module_3_1_ff6, module_3_1_led3, module_3_1_out;

  Clock clock_1 (.out(clock_1_out));
  Button button_1 (.out(button_1_out));
  Button button_2 (.out(button_2_out));
  Module_1 module_1_1 (
    .CLK(clock_1_out), .CLR(button_2_out), .L7(module_3_1_out), .L6(module_3_1_ff6), .Q(module_1_1_q),
    .QN(module_1_1_qn), .LED1(module_1_1_led1), .LED0(module_1_1_led0), .PST(module_3_1_out),
    .IN(button_1_out));  // open: FF0, FF1
  LED led_1 (.in(module_1_1_led0));
  LED led_2 (.in(module_1_1_led1));
  LED led_3 (.in(module_3_1_led3));
  LED led_4 (.in(module_2_1_led2));
  Module_2 module_2_1 (
    .CLK(clock_1_out), .J(module_1_1_q), .K(module_1_1_qn), .CLR(button_2_out), .L5(module_3_1_ff5),
    .Q(module_2_1_q), .LED2(module_2_1_led2), .QN(module_2_1_qn), .FF3(module_2_1_ff3));  // open: FF2
  Module_3 module_3_1 (
    .CLK(clock_1_out), .J(module_2_1_q), .K(module_2_1_qn), .CLR(button_2_out), .L4(module_2_1_ff3),
    .OUT(module_3_1_out), .LED3(module_3_1_led3), .FF6(module_3_1_ff6), .FF5(module_3_1_ff5));  // open: OUTN, FF4
endmodule

module Ex__4bit_led (
);

  wire button_1_out, clock_1_out, j_k_ff_1_qn, j_k_ff_2_qn, j_k_ff_3_qn, j_k_ff_4_qn, j_k_ff_5_qn,
       j_k_ff_6_qn, j_k_ff_7_qn, not_1_out, or_1_out, or_2_out, or_3_out, or_4_out, or_5_out, undriven;
  wire [3:0] j_k_ff_1_q, j_k_ff_5_q;

  Clock clock_1 (.out(clock_1_out));
  or or_1 (or_1_out, button_1_out, j_k_ff_5_q[3]);
  Button button_1 (.out(button_1_out));
  not not_1 (not_1_out, or_1_out);
  J_K_Flip_Flop j_k_ff_1 (
    .J(or_1_out), .clk(clock_1_out), .K(not_1_out), .Q(j_k_ff_1_q[0]), .Qn(j_k_ff_1_qn), .reset(undriven));  // open: preset, en
  J_K_Flip_Flop j_k_ff_2 (
    .J(j_k_ff_1_q[0]), .clk(clock_1_out), .K(j_k_ff_1_qn), .Q(j_k_ff_1_q[1]), .Qn(j_k_ff_2_qn),
    .reset(undriven));  // open: preset, en
  J_K_Flip_Flop j_k_ff_3 (
    .J(j_k_ff_1_q[1]), .clk(clock_1_out), .K(j_k_ff_2_qn), .Q(j_k_ff_1_q[2]), .Qn(j_k_ff_3_qn),
    .reset(undriven));  // open: preset, en
  J_K_Flip_Flop j_k_ff_4 (
    .J(j_k_ff_1_q[2]), .clk(clock_1_out), .K(j_k_ff_3_qn), .Q(j_k_ff_1_q[3]), .Qn(j_k_ff_4_qn),
    .reset(undriven));  // open: preset, en
  J_K_Flip_Flop j_k_ff_5 (
    .J(j_k_ff_1_q[3]), .clk(clock_1_out), .K(j_k_ff_4_qn), .Q(j_k_ff_5_q[0]), .Qn(j_k_ff_5_qn),
    .reset(undriven));  // open: preset, en
  J_K_Flip_Flop j_k_ff_6 (
    .J(j_k_ff_5_q[0]), .clk(clock_1_out), .K(j_k_ff_5_qn), .Q(j_k_ff_5_q[1]), .Qn(j_k_ff_6_qn),
    .reset(undriven));  // open: preset, en
  or or_2 (or_2_out, j_k_ff_1_q[1], j_k_ff_5_q[2]);
  or or_3 (or_3_out, j_k_ff_1_q[0], j_k_ff_5_q[3]);
  LED led_1 (.in(or_3_out));
  LED led_2 (.in(or_5_out));
  LED led_3 (.in(or_2_out));
  J_K_Flip_Flop j_k_ff_7 (
    .J(j_k_ff_5_q[1]), .clk(clock_1_out), .K(j_k_ff_6_qn), .Q(j_k_ff_5_q[2]), .Qn(j_k_ff_7_qn),
    .reset(undriven));  // open: preset, en
  or or_4 (or_4_out, j_k_ff_1_q[3], j_k_ff_5_q[0]);
  or or_5 (or_5_out, j_k_ff_1_q[2], j_k_ff_5_q[1]);
  LED led_4 (.in(or_4_out));
  J_K_Flip_Flop j_k_ff_8 (
    .J(j_k_ff_5_q[2]), .clk(clock_1_out), .K(j_k_ff_7_qn), .Q(j_k_ff_5_q[3]), .reset(undriven));  // open: Qn, preset, en

  // Notes on the sheet:
  //   CLK
  //   IN
endmodule
