// Logisim project shift-register.circ as structural Verilog: 1 circuit, main circuit main
module main (
);

  wire j_k_ff_1_qn, j_k_ff_2_qn, j_k_ff_3_qn, j_k_ff_4_qn, j_k_ff_5_qn, j_k_ff_6_qn, j_k_ff_7_qn, not_1_out,
       undriven, undriven_2, undriven_3;
  wire [7:0] j_k_ff_1_q;

  not not_1 (not_1_out, undriven);
  J_K_Flip_Flop j_k_ff_1 (
    .J(undriven), .clk(undriven_2), .K(not_1_out), .Q(j_k_ff_1_q[0]), .Qn(j_k_ff_1_qn), .reset(undriven_3));  // open: preset, en
  J_K_Flip_Flop j_k_ff_2 (
    .J(j_k_ff_1_q[0]), .clk(undriven_2), .K(j_k_ff_1_qn), .Q(j_k_ff_1_q[1]), .Qn(j_k_ff_2_qn),
    .reset(undriven_3));  // open: preset, en
  J_K_Flip_Flop j_k_ff_3 (
    .J(j_k_ff_1_q[1]), .clk(undriven_2), .K(j_k_ff_2_qn), .Q(j_k_ff_1_q[2]), .Qn(j_k_ff_3_qn),
    .reset(undriven_3));  // open: preset, en
  J_K_Flip_Flop j_k_ff_4 (
    .J(j_k_ff_1_q[2]), .clk(undriven_2), .K(j_k_ff_3_qn), .Q(j_k_ff_1_q[3]), .Qn(j_k_ff_4_qn),
    .reset(undriven_3));  // open: preset, en
  J_K_Flip_Flop j_k_ff_5 (
    .J(j_k_ff_1_q[3]), .clk(undriven_2), .K(j_k_ff_4_qn), .Q(j_k_ff_1_q[4]), .Qn(j_k_ff_5_qn),
    .reset(undriven_3));  // open: preset, en
  J_K_Flip_Flop j_k_ff_6 (
    .J(j_k_ff_1_q[4]), .clk(undriven_2), .K(j_k_ff_5_qn), .Q(j_k_ff_1_q[5]), .Qn(j_k_ff_6_qn),
    .reset(undriven_3));  // open: preset, en
  J_K_Flip_Flop j_k_ff_7 (
    .J(j_k_ff_1_q[5]), .clk(undriven_2), .K(j_k_ff_6_qn), .Q(j_k_ff_1_q[6]), .Qn(j_k_ff_7_qn),
    .reset(undriven_3));  // open: preset, en
  J_K_Flip_Flop j_k_ff_8 (
    .J(j_k_ff_1_q[6]), .clk(undriven_2), .K(j_k_ff_7_qn), .Q(j_k_ff_1_q[7]), .reset(undriven_3));  // open: Qn, preset, en

  // Notes on the sheet:
  //   Output
  //   Last
  //   CLK
  //   RESET
  //   IN
endmodule
