// Logisim project test.circ as structural Verilog: 1 circuit, main circuit main
module main (
);

  wire button_1_out, button_2_out, clock_1_out, d_ff_1_q, or_1_out, or_2_out, or_3_out, or_4_out, or_5_out,
       or_6_out, or_7_out, or_8_out, or_9_out, shift_register_1_out, shift_register_1_q0,
       shift_register_1_q1, shift_register_1_q2, shift_register_1_q3, shift_register_1_q4,
       shift_register_1_q5, shift_register_1_q6, shift_register_1_q7, shift_register_2_out,
       shift_register_2_q0, shift_register_2_q1, shift_register_2_q2, shift_register_2_q3,
       shift_register_2_q4, shift_register_2_q5, shift_register_2_q6, shift_register_2_q7;

  // Probe on d_ff_1_q
  Button button_1 (.out(button_1_out));
  D_Flip_Flop d_ff_1 (.clk(clock_1_out), .D(1'b0), .Q(d_ff_1_q), .preset(button_1_out));  // open: Qn, en, reset
  Clock clock_1 (.out(clock_1_out));
  or or_1 (or_1_out, d_ff_1_q, shift_register_2_out);
  Shift_Register shift_register_1 (
    .in(or_1_out), .clk(clock_1_out), .out(shift_register_1_out), .clr(button_2_out),
    .q0(shift_register_1_q0), .q1(shift_register_1_q1), .q2(shift_register_1_q2), .q3(shift_register_1_q3),
    .q4(shift_register_1_q4), .q5(shift_register_1_q5), .q6(shift_register_1_q6), .q7(shift_register_1_q7));  // open: shift, load, d0, d1, d2, d3, d4, d5, d6, d7
  Button button_2 (.out(button_2_out));
  or or_2 (or_2_out, shift_register_1_q0, shift_register_2_q7);
  or or_3 (or_3_out, shift_register_1_q1, shift_register_2_q6);
  or or_4 (or_4_out, shift_register_1_q2, shift_register_2_q5);
  or or_5 (or_5_out, shift_register_1_q3, shift_register_2_q4);
  LED led_1 (.in(or_3_out));
  LED led_2 (.in(or_5_out));
  LED led_3 (.in(or_2_out));
  LED led_4 (.in(or_4_out));
  or or_6 (or_6_out, shift_register_1_q4, shift_register_2_q3);
  LED led_5 (.in(or_8_out));
  LED led_6 (.in(or_6_out));
  LED led_7 (.in(or_9_out));
  LED led_8 (.in(or_7_out));
  Shift_Register shift_register_2 (
    .in(shift_register_1_out), .clk(clock_1_out), .out(shift_register_2_out), .clr(button_2_out),
    .q0(shift_register_2_q0), .q1(shift_register_2_q1), .q2(shift_register_2_q2), .q3(shift_register_2_q3),
    .q4(shift_register_2_q4), .q5(shift_register_2_q5), .q6(shift_register_2_q6), .q7(shift_register_2_q7));  // open: shift, load, d0, d1, d2, d3, d4, d5, d6, d7
  or or_7 (or_7_out, shift_register_1_q6, shift_register_2_q1);
  or or_8 (or_8_out, shift_register_1_q5, shift_register_2_q2);
  or or_9 (or_9_out, shift_register_1_q7, shift_register_2_q0);
endmodule
